# Fritzing sketch Atari Punk dos (saved by Fritzing 0.9.2b)
circuit board: 5.46263cm x 6.0184cm
breadboards: 1

parts:
  U1 = 556 [package=dil14]
  R1 = Resistor [tolerance=±5% resistance=1k package=THT]
  C1 = Ceramic Capacitor [capacitance=100nF package="100 mil [THT, multilayer]"]
  C2 = Ceramic Capacitor [capacitance=100nF package="100 mil [THT, multilayer]"]
  C3 = Electrolytic Capacitor [capacitance=1µF package="100 mil [THT, electrolytic]"]
  0 = Screw terminal - 2 pins [package=THT]
  VCC3 = Battery
  R4 = Rotary Potentiometer (Large) [maximum_resistance=100kΩ package=THT]
  R5 = Rotary Potentiometer (Large) [maximum_resistance=100kΩ package=THT]

nets:
  N1: U1.DIS, R1.Pin_1, R4.leg2
  N2: U1.THR, U1.TRIG, R1.Pin_0, C1.1
  5V: U1.RST, U1.RST2, U1.VCC, 0.pin1, VCC3.+, R4.wiper, R5.wiper
  N3: U1.OUT, U1.TRIG2
  GND: U1.GND, C1.0, C2.0, VCC3.-
  N4: U1.OUT2, C3.-
  N5: U1.THR2, U1.DIS2, C2.1, R5.leg2
  N6: C3.+, 0.pin2

notes:
  Elephant
  Electronics
  Punk
